// Logisim project TN2.circ as structural Verilog: 1 circuit, main circuit main
module main (
  input  x,
  input  y,
  input  z,
  output out_4,
  output out_5,
  output out_6,
  output out_7,
  output out_8
);

  wire and_1_out, and_2_out, and_3_out, and_4_out, and_5_out, and_6_out, and_7_out, not_1_out, not_2_out,
       not_3_out, not_4_out, not_5_out, not_6_out, not_7_out, not_8_out, or_1_out, or_2_out, or_3_out,
       or_4_out, or_5_out, or_6_out, or_7_out;

  or or_1 (or_1_out, x, y);
  and and_1 (and_1_out, x, y);
  and and_2 (and_2_out, y, z);
  not not_1 (not_1_out, x);
  not not_2 (not_2_out, x);
  not not_3 (not_3_out, or_1_out);
  not not_4 (not_4_out, and_1_out);
  or or_2 (or_2_out, x, and_2_out);
  and and_3 (and_3_out, not_1_out, y);
  and and_4 (and_4_out, not_2_out, y);
  or or_3 (or_3_out, x, and_3_out);
  or or_4 (or_4_out, x, and_4_out);
  not not_5 (not_5_out, x);
  not not_6 (not_6_out, y);
  not not_7 (not_7_out, x);
  not not_8 (not_8_out, y);
  or or_5 (or_5_out, x, y);
  or or_6 (or_6_out, x, z);
  or or_7 (or_7_out, x, y);
  and and_5 (and_5_out, not_5_out, not_6_out);
  and and_6 (and_6_out, not_7_out, not_8_out);
  and and_7 (and_7_out, or_5_out, or_6_out);
  xnor xnor_1 (out_4, not_3_out, and_5_out);
  xnor xnor_2 (out_5, not_4_out, and_6_out);
  xnor xnor_3 (out_6, or_2_out, and_7_out);
  xnor xnor_4 (out_8, or_4_out, or_7_out);
  xnor xnor_5 (out_7, or_3_out, x);

  // Notes on the sheet:
  //   EQ1
  //   EQ2
  //   EQ3
  //   EQ4
  //   EQ5
endmodule
